# Fritzing sketch schematics (saved by Fritzing 0.9.6b)
breadboards: 1

parts:
  R1 = Resistor [tolerance=±5% power=0.25 resistance=10k package=THT]
  U1 = ESP8266 WiFi Module [part_number=ESP8266]
  R2 = Resistor [tolerance=±5% power=0.25 resistance=10k package=THT]
  R3 = Resistor [tolerance=±5% power=0.25 resistance=10k package=THT]
  R4 = Resistor [tolerance=±5% power=0.25 resistance=10k package=THT]
  C1 = Capacitor Polarized [package=cpol-radial-10uf-25v]
  U2 = IC, SIP package, 3 pins [chip_label="DHT 11"]
  U3 = IC, SIP package, 4 pins [chip_label=SSD1306]
  U4 = IC, SIP package, 4 pins [chip_label=HW-103]
  S1 = SWITCH-MOMENTARY-2 [package=tactile_switch_tall]
  R5 = Resistor [tolerance=±5% power=0.25 resistance=470 package=THT]
  R6 = Resistor [tolerance=±5% power=0.25 resistance=100k package=THT]
  R7 = Resistor [tolerance=±5% power=0.25 resistance=220k package=THT]

nets:
  3.3V/VCC: R1.Pin_0, U1.VCC, R2.Pin_0, R4.Pin_0, C1.+, U2.pin2, U3.pin4, U4.pin4, S1.1
  N1: R1.Pin_1, U1.CH_PD
  N2: U1.GPIO_0, R2.Pin_1
  GPIO2: U1.GPIO_2, U2.pin1
  GND: U1.GND, R3.Pin_1, C1.-, U2.pin3, U3.pin3, U4.pin3, R5.Pin_1, R6.Pin_1
  N3: U1.GPIO_15, R3.Pin_0
  N4: U1.GPIO_4, U3.pin1
  N5: U1.GPIO_5, U3.pin2
  ADC: U1.ADC_0, R6.Pin_0, R7.Pin_1
  GPIO16: U1.GPIO_16
  GPIO12: U1.GPIO_12, S1.2, R5.Pin_0
  N6: U1.REST, R4.Pin_1
  VD_IN: U4.pin1, R7.Pin_0
